# Fritzing sketch dht22 (saved by Fritzing 0.9.2b)
circuit board: 8.46667cm x 5.64444cm
breadboards: 1

parts:
  R1 = Resistor [tolerance=±5% resistance=10k package=THT]
  DHT_22 = Humidity and Temperature Sensor RHT03
  U1 = ESP32S-HiLetgo [part_number=ESP32]

nets:
  N1: R1.Pin_0, DHT_22.Vcc, U1.3.3
  N2: R1.Pin_1, DHT_22.Data-signal, U1.GPIO2
  N3: DHT_22.GND_2, U1.GND

custom parts:
  ESP32S-HiLetgo: HiLetgo ESP-WROOM-32 ESP32 ESP-32S Development Board 2.4GHz Dual-Mode WiFi + Bluetooth Dual Cores Microcontroller The ESP32 integrated with Antenna switches, RF Balun, power amplifiers, low-noise amplifiers, filters, and management modules, and the entire solution occupies the least area of PCB. 2.4 GHz Wi-Fi plus Bluetooth dual-mode chip, with TSMC Ultra-low power consumption 40nm technology,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
