# Fritzing sketch reed (saved by Fritzing 0.9.2b)
breadboards: 1

parts:
  U1 = NodeMCU V1.0
  S1 = Reed switch [package=THT]
  R1 = Resistor [tolerance=±5% resistance=220 package=THT]

nets:
  N1: U1.D2, R1.Pin_1
  N2: U1.GND, S1.pin_2
  N3: S1.pin_1, R1.Pin_0

custom parts:
  NodeMCU V1.0: ESP8266 based NodeMCU
