# Fritzing sketch relay (saved by Fritzing 0.9.2b)
breadboards: 1

parts:
  U2 = 2-Channel 5v Relay Shield [package=relay-2ch5v10a]
  U3 = NodeMCU V1.0

nets:
  VCC: U2.VCC, U3.Vin
  GND: U2.GND, U3.GND
  N1: U2.IN1, U3.D2
  N2: U2.IN2, U3.D4

custom parts:
  2-Channel 5v Relay Shield: 2 Channel 5v Relay Shield w. 2x SPD-06VDC-SD-C
  NodeMCU V1.0: ESP8266 based NodeMCU
